# Fritzing sketch Pumpkin (saved by Fritzing 0.9.3b)

parts:
  R1 = BBC MicroBit
  Part1 = NeoPixel Jewel [part_number=2226]

nets:
  GND: R1.GND, Part1.GND
  3V3: R1.3v3, Part1.VDD
  N1: R1.P0_ANALOG_IN, Part1.IN

custom parts:
  BBC MicroBit: The BBC MICRO:BIT
  NeoPixel Jewel: We fit seven of our tiny 5050 (5mm x 5mm) smart RGB LEDs onto a beautiful, round PCB with mounting holes and a chainable design to create what we think is our most elegant (and evening-wear appropriate) NeoPixel board yet. Use only one microcontroller pin to control as many as you can chain together! Each LED is addressable as the driver chip is inside the LED. Each one has ~18mA constant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
